# Fritzing sketch skema sensor (saved by Fritzing 0.9.3b)
breadboards: 1

parts:
  Part1 = Arduino Uno (Rev3)
  hc-sr1 = hc-sr04

nets:
  N1: Part1.D11_PWM/MOSI, hc-sr1.Echo
  N2: Part1.D12/MISO, hc-sr1.Trig
  GND: Part1.GND, hc-sr1.GND
  5V: Part1.5V, hc-sr1.VCC
